// Logisim project CPU-16IR.circ as structural Verilog: 17 circuits, main circuit mobo
module mobo (
);

  wire buffer_3_out, C_out, cpu_1_clk, cpu_1_interrupt, cpu_1_ram_write, I_O_out, keyboard_1_avail,
       keyboardextender_1_out_7, keyboardextender_1_out_9, or_1_out, or_2_out, powerbox_1_out_4,
       powerbox_1_out_5, pull_resistor_2_node, t_ff_1_qn, ttyextender_1_out_5, ttyextender_1_out_7;
  wire [3:0] keyboardextender_1_out_10;
  wire [6:0] keyboard_1_data, ttyextender_1_out_6;
  wire [7:0] counter_1_q;
  wire [15:0] cpu_1_address_bus, cpu_1_data_out, keyboardextender_1_out_11, ram_1_data;
  wire [31:0] cpu_1_hi_out, keyboardextender_1_out_8, keyboardextender_1_out_12;

  // Probe on ttyextender_1_out_6
  TTY #(.rows(12), .cols(50)) tty_1 (
    .data(ttyextender_1_out_6), .clk(cpu_1_clk), .we(ttyextender_1_out_7), .clr(ttyextender_1_out_5));
  TTYextender ttyextender_1 (
    .in_2(keyboardextender_1_out_12), .in_1(cpu_1_clk), .in_3(keyboardextender_1_out_11),
    .in_4(keyboardextender_1_out_9), .out_6(ttyextender_1_out_6), .out_5(ttyextender_1_out_5),
    .out_7(ttyextender_1_out_7));
  Counter counter_1 (.Q(counter_1_q), .clr(keyboardextender_1_out_9));  // open: load, D, count, carry, clk
  Register register_1 (.D(counter_1_q), .clk(keyboardextender_1_out_9));  // open: en, Q, clr
  ROM #(.addrWidth(16), .dataWidth(16)) rom_1 ();  // open: addr, data, sel
  Button I_O (.out(I_O_out));
  Keyboard #(.buflen(256)) keyboard_1 (
    .clk(keyboardextender_1_out_7), .clr(C_out), .avail(keyboard_1_avail), .data(keyboard_1_data));  // open: re
  Button C (.out(C_out));
  KeyboardExtender keyboardextender_1 (
    .out_7(keyboardextender_1_out_7), .in_1(keyboard_1_data), .in_2(keyboard_1_avail), .in_3(cpu_1_clk),
    .in_4(keyboardextender_1_out_12), .out_8(keyboardextender_1_out_8), .in_5(keyboardextender_1_out_11),
    .out_11(keyboardextender_1_out_11), .in_6(keyboardextender_1_out_9), .out_9(keyboardextender_1_out_9),
    .out_10(keyboardextender_1_out_10), .out_12(keyboardextender_1_out_12));
  PowerBox powerbox_1 (
    .in_1(keyboardextender_1_out_11), .INT(keyboardextender_1_out_9), .in_3(keyboardextender_1_out_12),
    .out_4(powerbox_1_out_4), .out_5(powerbox_1_out_5));
  or or_1 (or_1_out, powerbox_1_out_4, I_O_out);
  T_Flip_Flop t_ff_1 (.clk(or_1_out), .T(or_1_out), .Qn(t_ff_1_qn));  // open: Q, preset, reset, en
  or or_2 (or_2_out, powerbox_1_out_5, t_ff_1_qn);
  Pull_Resistor pull_resistor_1 (.node(keyboardextender_1_out_10));
  assign keyboardextender_1_out_11 = pull_resistor_2_node ? cpu_1_address_bus : 16'bz;  // Controlled_Buffer controlled_buffer_1
  Pull_Resistor pull_resistor_2 (.node(pull_resistor_2_node));
  buf buffer_1 (pull_resistor_2_node, cpu_1_interrupt);
  CPU cpu_1 (
    .Data_IN(ram_1_data), .Address_bus(cpu_1_address_bus), .Data_OUT(cpu_1_data_out), .CLK(cpu_1_clk),
    .RAM_write(cpu_1_ram_write), .HI_out(cpu_1_hi_out), .LO_in(keyboardextender_1_out_8),
    .INT_return(keyboardextender_1_out_10), .BOOT(or_2_out), .interrupt(cpu_1_interrupt));
  Pull_Resistor pull_resistor_3 (.node(keyboardextender_1_out_9));
  buf buffer_2 (keyboardextender_1_out_9, cpu_1_interrupt);
  buf buffer_3 (buffer_3_out, cpu_1_interrupt);
  Pull_Resistor pull_resistor_4 (.node(buffer_3_out));
  assign keyboardextender_1_out_12 = buffer_3_out ? cpu_1_hi_out : 32'bz;  // Controlled_Buffer controlled_buffer_2
  RAM #(.addrWidth(16), .dataWidth(16), .bus("separate")) ram_1 (
    .addr(cpu_1_address_bus), .din(cpu_1_data_out), .data(ram_1_data), .str(cpu_1_ram_write), .clk(cpu_1_clk));  // open: sel, ld, clr

  // Notes on the sheet:
  //   fibonacci example
  //   contents of rom_1 (hex, n*v repeats v):
  //   e4e0 f000 800 15c 800 2f 40*78 3 e3e8 14e0 1 e3e9 14e0 1 e3ea 14e0 1 e3eb 14e0 1 e3ed 14e0 1 e3ec
  //   14e0 1 e3ef 14e0 1 f000 11e0 1 e2fe 11e0 1 e2ce 11e0 1 e2de 11e0 1 e2be 11e0 1 e2ae 11e0 1 e29e 11e0
  //   1 e28e f000 f100 2f e440 a e450 30 6dd 6cc e7f8 2394 e77f 384 475 e3e7 14e0 1 14c0 1 e7b8 5b9 e6bd
  //   1900 63 11e0 1 e20e e500 1 11c0 1 e6cd b00 72 f100 45 f000 f100 2f 699 6dd e430 a e450 30 383 e74f
  //   445 e3e4 14e0 1 14d0 1 e628 1900 87 699 11e0 1 e20e e500 1 11d0 1 e6d9 b00 93 f100 45 f000 f100 2f
  //   e420 3 e7dc e20c e602 900 af e500 1 14c0 1 800 a5 1dc 17d0 0 14d0 1 f100 45 f000 f100 2f e7de e4e0 6
  //   688 e400 1 e500 2 e7be 655 e651 900 bd e450 8 e651 1900 d4 11e0 1 e25e e7be e701 e500 1 800 bd e4a0
  //   6 14a0 28 e6ea d00 bd e450 a e651 900 ee e450 d e651 900 ee e701 e3e0 14e0 1 e7be e500 1 800 bd e400
  //   3 e3e0 14e0 1 e400 a e500 1 e7ed f100 45 f000 f100 2f e440 1 e460 3 e258 e279 484 494 e657 1900 110
  //   e656 1900 101 f100 45 e410 1 f000 f100 45 611 f000 800 118 78 3 800 11c 78 3 800 12f 78 78 78 2e 78
  //   78 78 2e 78 78 78 2e 4*78 3 e108 11a f000 e3eb 14e0 1 6bb 14b0 1 e69b b00 136 11e0 1 e2be f000 800
  //   15c 80 42 49 4f 53 20 62 6f 6f 74 65 64 20 73 75 63 63 65 73 73 66 75 6c 6c 79 a 3 e4c0 141 f100 a0
  //   800 1e2 800 19d a 54 68 69 73 20 70 72 6f 67 72 61 6d 20 63 61 6c 63 75 6c 61 74 65 73 20 61 6c 6c
  //   20 33 32 2d 62 69 74 20 46 69 62 62 6f 6e 61 63 63 69 a 6e 75 6d 62 65 72 73 2e a 3 800 1d2 50*2d 3
  //   800 1df 54 68 65 72 65 20 61 72 65 20 3 800 1e2 0 e080 1e1 e490 0 e689 900 205 e4c0 1d4 f100 a0 f100
  //   7f 600 e100 1e1 e400 a e500 1 e4c0 19f f100 a0 e400 a e500 1 688 699 6aa e4b0 1 800 215 e480 0 e490
  //   0 e4a0 0 e4b0 1 e4c0 164 f100 a0 e4c0 19f f100 a0 49b 248a e68a a00 1e2 e3e8 14e0 1 e3e9 14e0 1 e78a
  //   e79b 11e0 1 e2be 11e0 1 e2ae f100 5b e3e8 14e0 1 e080 1e1 1480 1 e108 1e1 e400 a e500 1 11e0 1 e28e
  //   800 215
  //   CLICK THE KEYBOARD
  //   TO TYPE
  //   <
  //   <
  //   INTx46
  //   RAM
endmodule

module CPU (
  input  [15:0] Data_IN,
  input  [31:0] LO_in,
  input  BOOT,
  input  [3:0] INT_return,
  output [31:0] HI_out,
  output CLK,
  output RAM_write,
  output interrupt,
  output [15:0] Data_OUT,
  output [15:0] Address_bus
);

  wire and_1_out, call, d_ff_1_q, decod_1_immed_alu, decod_1_interrupt, decod_1_out_11, decod_1_regw,
       decod_1_rem_feed, decod_1_rem_set, jmp, or_2_out, pc_plus_plus, ret;
  wire [1:0] decod_1_out_7, decod_1_out_10;
  wire [2:0] decod_1_alu_operator;
  wire [3:0] dreg, or_1_out, sreg;
  wire [7:0] adder_1_out, alu_1_flags, csp_q, Flags_q, multiplexer_3_out;
  wire [15:0] alu_1_c_out, alu_1_result_q, buffer_1_out, controlled_buffer_1_out, Immed_q,
       increment16bit_1_out_2, multiplexer_1_out, multiplexer_2_out, multiplexer_4_out, Program_Counter_q,
       ram_1_data, registers_1_dbus, registers_1_rem_out;

  Multiplexer #(.select(2), .width(16), .enable("false")) multiplexer_1 (
    .in0(Immed_q), .in1(Data_OUT), .in2(Data_IN), .in3(alu_1_result_q), .out(multiplexer_1_out),
    .sel(decod_1_out_7));
  Multiplexer #(.width(16), .enable("false")) multiplexer_2 (
    .in0(Immed_q), .in1(ram_1_data), .out(multiplexer_2_out), .sel(d_ff_1_q));
  assign or_1_out = INT_return | dreg;  // OR_Gate or_1, 4 bits wide
  Registers registers_1 (
    .Data_in(multiplexer_1_out), .dregsel(or_1_out), .dbus(registers_1_dbus), .sbus(Data_OUT),
    .regw(decod_1_regw), .sregsel(sreg), .rem_set(decod_1_rem_set), .Rem_in(buffer_1_out),
    .Rem_out(registers_1_rem_out), .INT_in(LO_in), .INT_out(HI_out), .Reset(BOOT), .INT(decod_1_interrupt),
    .CLK(CLK));
  assign buffer_1_out = alu_1_c_out;  // Buffer buffer_1, 16 bits wide
  D_Flip_Flop d_ff_1 (.clk(CLK), .D(ret), .Q(d_ff_1_q));  // open: Qn, preset, en, reset
  assign controlled_buffer_1_out = decod_1_rem_feed ? registers_1_rem_out : 16'bz;  // Controlled_Buffer controlled_buffer_1
  ALU alu_1 (
    .A(registers_1_dbus), .B(multiplexer_4_out), .op(decod_1_alu_operator), .result_Q(alu_1_result_q),
    .C_IN(controlled_buffer_1_out), .C_OUT(alu_1_c_out), .FLAGS(alu_1_flags), .reset(BOOT));
  and and_1 (and_1_out, ~jmp, pc_plus_plus);  // AND_Gate
  Multiplexer #(.width(8), .enable("false")) multiplexer_3 (
    .in0(8'h1), .in1({8{1'b1}}), .out(multiplexer_3_out), .sel(ret));
  Register #(.width(16)) Immed (.D(Data_IN), .en(decod_1_out_11), .Q(Immed_q), .clk(CLK), .clr(BOOT));
  Multiplexer #(.width(16), .enable("false")) multiplexer_4 (
    .in0(Data_OUT), .in1(Immed_q), .out(multiplexer_4_out), .sel(decod_1_immed_alu));
  Counter #(.width(16), .max('hffff)) Program_Counter (
    .load(jmp), .D(multiplexer_2_out), .count(and_1_out), .Q(Program_Counter_q), .clk(CLK), .clr(BOOT));  // open: carry
  Register csp (.D(adder_1_out), .en(or_2_out), .Q(csp_q), .clk(CLK), .clr(BOOT));
  Adder adder_1 (.a(multiplexer_3_out), .b(csp_q), .out(adder_1_out));  // open: cin, cout
  or or_2 (or_2_out, ret, call);
  increment16bit increment16bit_1 (.in_1(Program_Counter_q), .out_2(increment16bit_1_out_2));
  Register Flags (.D(alu_1_flags), .en(decod_1_rem_set), .Q(Flags_q), .clk(CLK), .clr(BOOT));
  Multiplexer #(.select(2), .width(16), .enable("false")) multiplexer_5 (
    .in0(Program_Counter_q), .in1(Immed_q), .in2(Data_OUT), .in3(registers_1_dbus), .out(Address_bus),
    .sel(decod_1_out_10));
  Decod decod_1 (
    .out_11(decod_1_out_11), .Instruction(Data_IN), .regw(decod_1_regw), .rem_feed(decod_1_rem_feed),
    .out_6(dreg), .RAM_w(RAM_write), .Flags(Flags_q), .out_17(jmp), .out_10(decod_1_out_10),
    .out_7(decod_1_out_7), .in_2(BOOT), .out_5(sreg), .immed_alu(decod_1_immed_alu), .pcnext(pc_plus_plus),
    .ALU_OPERATOR(decod_1_alu_operator), .interrupt(decod_1_interrupt), .out_19(call), .out_20(ret),
    .in_3(CLK), .rem_set(decod_1_rem_set));
  buf buffer_2 (interrupt, decod_1_interrupt);
  // Probe on Data_OUT
  // Probe on Address_bus
  RAM #(.dataWidth(16), .bus("separate")) ram_1 (
    .addr(csp_q), .din(increment16bit_1_out_2), .data(ram_1_data), .str(call), .clk(CLK));  // open: sel, ld, clr
  Clock clock_1 (.out(CLK));

  // Notes on the sheet:
  //   Perip. bus
  //   RBus
  //   IBus
  //   DBus
  //   SBus
  //   buffer_2 drives only 1 and floats otherwise
  //   CALL STACK
endmodule

module Decod (
  input  [15:0] Instruction,
  input  in_2,
  input  in_3,
  input  [7:0] Flags,
  output [3:0] out_5,
  output [3:0] out_6,
  output [1:0] out_7,
  output immed_alu,
  output pcnext,
  output [1:0] out_10,
  output out_11,
  output [2:0] ALU_OPERATOR,
  output regw,
  output rem_feed,
  output rem_set,
  output RAM_w,
  output out_17,
  output interrupt,
  output out_19,
  output out_20
);

  wire and_1_out, and_3_out, and_5_out, and_6_out, and_8_out, buffer_1_out, buffer_2_out, d_ff_1_q, d_ff_2_q,
       demultiplexer_1_out0, demultiplexer_1_out1, demultiplexer_1_out2, demultiplexer_1_out3, imm, \int ,
       jmp, multiplexer_4_out, multiplexer_6_out, multiplexer_7_out, multiplexer_10_out, nor_1_out, \not ,
       not_1_out, not_2_out, not_3_out, or_1_out, or_2_out, or_3_out, or_4_out, or_5_out, or_6_out, or_7_out,
       or_8_out, pop, push, ramaccess, ramw, regw_t;
  wire [1:0] adrsel, phase;
  wire [7:3] register_1_q;
  wire [15:12] rom_1_data;

  Multiplexer #(.select(2), .disabled(0), .enable("false")) multiplexer_1 (
    .in1(imm), .out(out_11), .sel(phase));  // open: in0, in2, in3
  Multiplexer #(.select(2), .disabled(0), .enable("false")) multiplexer_2 (
    .in0(1'b0), .in1(1'b0), .in2(ramw), .in3(1'b0), .out(RAM_w), .sel(phase));
  Pull_Resistor pull_resistor_1 (.node(interrupt));
  Multiplexer #(.select(2), .disabled(0), .enable("false")) multiplexer_3 (
    .in2(\int ), .out(interrupt), .sel(phase));  // open: in0, in1, in3
  Register #(.width(16)) register_1 (
    .D(Instruction), .en(multiplexer_4_out), .Q({register_1_q, ALU_OPERATOR, out_6, out_5}), .clk(in_3),
    .clr(in_2));
  Pull_Resistor pull_resistor_2 (.node({register_1_q, ALU_OPERATOR, out_6, out_5}));
  Pull_Resistor pull_resistor_3 (.node(out_11));
  nor nor_1 (nor_1_out, Flags[1], Flags[0]);
  Multiplexer #(.select(2), .enable("false")) multiplexer_4 (
    .in0(1'b1), .out(multiplexer_4_out), .sel(phase));  // open: in1, in2, in3
  Pull_Resistor pull_resistor_4 (.node(multiplexer_4_out));
  // Probe on phase
  or or_1 (or_1_out, Flags[0], Flags[1]);
  or or_2 (or_2_out, nor_1_out, Flags[1]);
  ROM #(.dataWidth(16)) rom_1 (
    .addr({register_1_q, ALU_OPERATOR}),
    .data({rom_1_data, push, pop, \int , imm, \not , jmp, regw_t, ramw, adrsel, out_7}));  // open: sel
  Multiplexer #(.select(2), .width(2), .disabled(0), .enable("false")) multiplexer_5 (
    .in0(2'b00), .in1(2'b00), .in2(adrsel), .in3(2'b00), .out(out_10), .sel(phase));
  Multiplexer #(.select(2), .disabled(0), .enable("false")) multiplexer_6 (
    .in0(1'b0), .in1(regw_t), .in2(1'b0), .in3(1'b0), .out(multiplexer_6_out), .sel(phase));
  or or_3 (or_3_out, ramaccess, imm);
  Multiplexer #(.select(3), .disabled(0), .enable("false")) multiplexer_7 (
    .in0(1'b1), .in1(Flags[1]), .in2(nor_1_out), .in3(Flags[0]), .in4(or_2_out), .in5(or_1_out),
    .in6(Flags[2]), .in7(Flags[3]), .out(multiplexer_7_out), .sel(ALU_OPERATOR));
  Multiplexer #(.select(2), .disabled(0), .enable("false")) multiplexer_8 (
    .in1(push), .out(out_19), .sel(phase));  // open: in0, in2, in3
  Pull_Resistor pull_resistor_5 (.node(out_19));
  and and_1 (and_1_out, out_7[0], out_7[1]);
  // AND_Gate and_2 has open pins: in0=out_7[0], in1=out_7[1], in2=imm, out=open
  Multiplexer #(.disabled(0), .enable("false")) multiplexer_9 (
    .in0(multiplexer_6_out), .in1(d_ff_1_q), .out(regw), .sel(or_3_out));
  D_Flip_Flop d_ff_1 (.clk(in_3), .D(multiplexer_6_out), .Q(d_ff_1_q), .reset(not_1_out));  // open: Qn, preset, en
  not not_1 (not_1_out, or_3_out);
  Multiplexer #(.enable("false")) multiplexer_10 (
    .in0(multiplexer_7_out), .in1(not_2_out), .out(multiplexer_10_out), .sel(\not ));
  not not_2 (not_2_out, multiplexer_7_out);
  or or_4 (or_4_out, and_3_out, buffer_1_out);
  and and_3 (and_3_out, in_3, ~in_2);  // AND_Gate
  or or_5 (or_5_out, adrsel[0], adrsel[1]);
  and and_4 (ramaccess, or_5_out, ~and_1_out);  // AND_Gate
  and and_5 (and_5_out, imm, ~jmp, \not );  // AND_Gate
  and and_6 (and_6_out, jmp, multiplexer_10_out);
  Counter #(.width(2), .max('h2)) counter_1 (
    .load(in_2), .D(2'b00), .count(and_3_out), .Q(phase), .clk(or_4_out), .clr(and_8_out));  // open: carry
  buf buffer_1 (buffer_1_out, buffer_2_out);
  buf buffer_2 (buffer_2_out, in_2);
  Demultiplexer #(.select(2), .disabled(0), .enable("false")) demultiplexer_1 (
    .out0(demultiplexer_1_out0), .out1(demultiplexer_1_out1), .out2(demultiplexer_1_out2),
    .out3(demultiplexer_1_out3), .in(1'b1), .sel(phase));
  Transistor transistor_1 (.in(and_5_out), .out(immed_alu), .gate(in_2));
  Pull_Resistor pull_resistor_6 (.node(immed_alu));
  Multiplexer #(.select(2), .disabled(0), .enable("false")) multiplexer_11 (
    .in0(1'b0), .in1(1'b0), .in2(1'b0), .in3(regw), .out(rem_feed), .sel(adrsel));
  and and_7 (rem_set, out_7[0], out_7[1]);
  or or_6 (or_6_out, and_6_out, push, pop);
  Multiplexer #(.select(2), .disabled(0), .enable("false")) multiplexer_12 (
    .in1(pop), .out(out_20), .sel(phase));  // open: in0, in2, in3
  and and_8 (and_8_out, demultiplexer_1_out2, not_3_out);
  not not_3 (not_3_out, or_7_out);
  LED led_1 (.in(demultiplexer_1_out0));
  LED led_2 (.in(demultiplexer_1_out1));
  or or_7 (or_7_out, or_8_out, d_ff_2_q);
  LED led_3 (.in(demultiplexer_1_out2));
  LED led_4 (.in(demultiplexer_1_out3));
  or or_8 (or_8_out, pop, jmp, ramaccess);
  Multiplexer #(.select(2), .disabled(0), .enable("false")) multiplexer_13 (
    .in2(or_6_out), .out(out_17), .sel(phase));  // open: in0, in1, in3
  Pull_Resistor pull_resistor_7 (.node(out_17));
  Pull_Resistor pull_resistor_8 (.node(out_20));
  D_Flip_Flop d_ff_2 (.clk(in_3), .D(or_8_out), .Q(d_ff_2_q), .reset(and_8_out));  // open: Qn, preset, en
  Multiplexer #(.select(2), .disabled(0), .enable("false")) multiplexer_14 (
    .in0(1'b1), .in1(imm), .in2(1'b0), .in3(1'b0), .out(pcnext), .sel(phase));

  // Other names for the same wires on the sheet: aluop[2:0] = ALU_OPERATOR; clock = in_3; dreg[3:0] = out_6;
  //   regsel[1:0] = out_7; reset = in_2; sreg[3:0] = out_5

  // Notes on the sheet:
  //   in_2: pull=down
  //   op1 meaning:
  //   changes "jump if" to "jump if not"
  //   Immed LOAD
  //   STORE
  //   ram > alu (but only when imm and not jmp)
  //   REG & ADR sel
  //   contents of rom_1 (hex, n*v repeats v):
  //   8*23 8*140 8*1a3 8*1c0 183 7*2f 184*0 126 114 2a 1c 120 304 3 21 8*0 400 940
  //   reg WRITE
  //   CALL/push
  //   PC LOAD (jmp)
  //   RAM > ALU
  //   rem feed
  //   rem set
  //   RET/pop
  //   PC ++
endmodule

module Registers (
  input  [15:0] Data_in,
  input  regw,
  input  [3:0] dregsel,
  input  [31:0] INT_in,
  input  [3:0] sregsel,
  input  INT,
  input  CLK,
  input  Reset,
  input  [15:0] Rem_in,
  input  rem_set,
  output [31:0] INT_out,
  output [15:0] dbus,
  output [15:0] sbus,
  output [15:0] Rem_out
);

  wire adder_1_out, and_1_out, demultiplexer_1_out0, demultiplexer_1_out1, demultiplexer_1_out2,
       demultiplexer_1_out3, demultiplexer_1_out4, demultiplexer_1_out5, demultiplexer_1_out6,
       demultiplexer_1_out7, demultiplexer_1_out8, demultiplexer_1_out9, demultiplexer_1_out10,
       demultiplexer_1_out11, demultiplexer_1_out12, demultiplexer_1_out13, demultiplexer_1_out14,
       demultiplexer_1_out15, int_t, not_1_out, not_2_out, not_3_out, not_4_out, or_1_out, or_2_out,
       or_3_out, or_4_out, or_5_out, or_6_out, or_7_out, or_8_out, or_9_out, or_10_out, pull_resistor_2_node;
  wire [3:0] controlled_buffer_1_out;
  wire [7:0] AL_q, bit_extender_1_out, BL_q, CL_q, DL_q, multiplexer_1_out, multiplexer_3_out,
       multiplexer_4_out, multiplexer_5_out, multiplexer_6_out;
  wire [15:0] adr_q, bit_extender_2_out, bit_extender_3_out, bit_extender_4_out, bit_extender_5_out,
       bit_extender_6_out, bit_extender_7_out, bit_extender_8_out, bit_extender_9_out, bp_q,
       multiplexer_2_out, pull_resistor_1_node, sp_q;

  D_Flip_Flop d_ff_1 (.clk(CLK), .D(INT), .Q(int_t));  // open: Qn, preset, en, reset
  // Probe on Rem_in
  Demultiplexer #(.select(4), .enable("false")) demultiplexer_1 (
    .out0(demultiplexer_1_out0), .out1(demultiplexer_1_out1), .out2(demultiplexer_1_out2),
    .out3(demultiplexer_1_out3), .out4(demultiplexer_1_out4), .out5(demultiplexer_1_out5),
    .out6(demultiplexer_1_out6), .out7(demultiplexer_1_out7), .out8(demultiplexer_1_out8),
    .out9(demultiplexer_1_out9), .out10(demultiplexer_1_out10), .out11(demultiplexer_1_out11),
    .out12(demultiplexer_1_out12), .out13(demultiplexer_1_out13), .out14(demultiplexer_1_out14),
    .out15(demultiplexer_1_out15), .in(regw), .sel(dregsel));
  and and_1 (and_1_out, regw, rem_set);
  Pull_Resistor pull_resistor_1 (.node(pull_resistor_1_node));
  Transistor #(.width(16)) transistor_1 (.in(Data_in), .out(pull_resistor_1_node), .gate(Reset));
  or or_1 (or_1_out, demultiplexer_1_out8, demultiplexer_1_out9, demultiplexer_1_out10, demultiplexer_1_out11);
  Multiplexer #(.width(8), .enable("false")) multiplexer_1 (
    .in0(pull_resistor_1_node[7:0]), .in1(pull_resistor_1_node[15:8]), .out(multiplexer_1_out), .sel(or_1_out));
  or or_2 (or_2_out, demultiplexer_1_out8, demultiplexer_1_out0);
  or or_3 (or_3_out, demultiplexer_1_out9, demultiplexer_1_out2);
  or or_4 (or_4_out, demultiplexer_1_out10, demultiplexer_1_out4);
  or or_5 (or_5_out, demultiplexer_1_out11, demultiplexer_1_out6);
  // Probe on multiplexer_1_out
  Multiplexer #(.width(16), .enable("false")) multiplexer_2 (
    .in0(pull_resistor_1_node), .in1(Rem_in), .out(multiplexer_2_out), .sel(and_1_out));
  or or_6 (or_6_out, and_1_out, demultiplexer_1_out15);
  Bit_Extender #(.in_width(16), .out_width(8)) bit_extender_1 (.in(pull_resistor_1_node), .out(bit_extender_1_out));
  Adder #(.width(1)) adder_1 (.a(int_t), .b(pull_resistor_2_node), .out(adder_1_out));  // open: cin, cout
  Pull_Resistor pull_resistor_2 (.node(pull_resistor_2_node));
  Register AH (.D(multiplexer_1_out), .en(or_2_out), .Q(INT_out[7:0]), .clk(CLK), .clr(Reset));
  Register BH (.D(multiplexer_1_out), .en(or_3_out), .Q(INT_out[15:8]), .clk(CLK), .clr(Reset));
  Register CH (.D(multiplexer_1_out), .en(or_4_out), .Q(INT_out[23:16]), .clk(CLK), .clr(Reset));
  Register DH (.D(multiplexer_1_out), .en(or_5_out), .Q(INT_out[31:24]), .clk(CLK), .clr(Reset));
  Register #(.width(16)) rm (.D(multiplexer_2_out), .en(or_6_out), .Q(Rem_out), .clk(CLK), .clr(Reset));
  Register #(.width(16)) adr (.D(pull_resistor_1_node), .en(demultiplexer_1_out12), .Q(adr_q), .clk(CLK), .clr(Reset));
  Register #(.width(16)) bp (.D(pull_resistor_1_node), .en(demultiplexer_1_out13), .Q(bp_q), .clk(CLK), .clr(Reset));
  Register #(.width(16)) sp (.D(pull_resistor_1_node), .en(demultiplexer_1_out14), .Q(sp_q), .clk(CLK), .clr(Reset));
  assign controlled_buffer_1_out = adder_1_out ? dregsel : 4'bz;  // Controlled_Buffer controlled_buffer_1
  Pull_Resistor pull_resistor_3 (.node(controlled_buffer_1_out));
  not not_1 (not_1_out, controlled_buffer_1_out[0]);
  not not_2 (not_2_out, controlled_buffer_1_out[1]);
  not not_3 (not_3_out, controlled_buffer_1_out[2]);
  not not_4 (not_4_out, controlled_buffer_1_out[3]);
  // Probe on bit_extender_1_out
  Multiplexer #(.width(8), .enable("false")) multiplexer_3 (
    .in0(INT_in[7:0]), .in1(bit_extender_1_out), .out(multiplexer_3_out), .sel(not_1_out));
  or or_7 (or_7_out, demultiplexer_1_out8, controlled_buffer_1_out[0], demultiplexer_1_out1);
  Multiplexer #(.width(8), .enable("false")) multiplexer_4 (
    .in0(INT_in[15:8]), .in1(bit_extender_1_out), .out(multiplexer_4_out), .sel(not_2_out));
  or or_8 (or_8_out, demultiplexer_1_out9, controlled_buffer_1_out[1], demultiplexer_1_out3);
  Multiplexer #(.width(8), .enable("false")) multiplexer_5 (
    .in0(INT_in[23:16]), .in1(bit_extender_1_out), .out(multiplexer_5_out), .sel(not_3_out));
  or or_9 (or_9_out, demultiplexer_1_out10, controlled_buffer_1_out[2], demultiplexer_1_out5);
  Multiplexer #(.width(8), .enable("false")) multiplexer_6 (
    .in0(INT_in[31:24]), .in1(bit_extender_1_out), .out(multiplexer_6_out), .sel(not_4_out));
  or or_10 (or_10_out, demultiplexer_1_out11, controlled_buffer_1_out[3], demultiplexer_1_out7);
  Register AL (.D(multiplexer_3_out), .en(or_7_out), .Q(AL_q), .clk(CLK), .clr(Reset));
  Register BL (.D(multiplexer_4_out), .en(or_8_out), .Q(BL_q), .clk(CLK), .clr(Reset));
  Register CL (.D(multiplexer_5_out), .en(or_9_out), .Q(CL_q), .clk(CLK), .clr(Reset));
  Register DL (.D(multiplexer_6_out), .en(or_10_out), .Q(DL_q), .clk(CLK), .clr(Reset));
  assign bit_extender_2_out = {{8{1'b0}}, INT_out[7:0]};  // Bit_Extender bit_extender_2
  assign bit_extender_3_out = {{8{1'b0}}, AL_q};  // Bit_Extender bit_extender_3
  assign bit_extender_4_out = {{8{1'b0}}, INT_out[15:8]};  // Bit_Extender bit_extender_4
  assign bit_extender_5_out = {{8{1'b0}}, BL_q};  // Bit_Extender bit_extender_5
  assign bit_extender_6_out = {{8{1'b0}}, INT_out[23:16]};  // Bit_Extender bit_extender_6
  assign bit_extender_7_out = {{8{1'b0}}, CL_q};  // Bit_Extender bit_extender_7
  assign bit_extender_8_out = {{8{1'b0}}, INT_out[31:24]};  // Bit_Extender bit_extender_8
  assign bit_extender_9_out = {{8{1'b0}}, DL_q};  // Bit_Extender bit_extender_9
  Multiplexer #(.select(4), .width(16), .disabled(0), .enable("false")) multiplexer_7 (
    .in0(bit_extender_2_out), .in1(bit_extender_3_out), .in2(bit_extender_4_out), .in3(bit_extender_5_out),
    .in4(bit_extender_6_out), .in5(bit_extender_7_out), .in6(bit_extender_8_out), .in7(bit_extender_9_out),
    .in8({INT_out[7:0], AL_q}), .in9({INT_out[15:8], BL_q}), .in10({INT_out[23:16], CL_q}),
    .in11({INT_out[31:24], DL_q}), .in12(adr_q), .in13(bp_q), .in14(sp_q), .in15(Rem_out), .out(dbus),
    .sel(dregsel));
  Multiplexer #(.select(4), .width(16), .disabled(0), .enable("false")) multiplexer_8 (
    .in0(bit_extender_2_out), .in1(bit_extender_3_out), .in2(bit_extender_4_out), .in3(bit_extender_5_out),
    .in4(bit_extender_6_out), .in5(bit_extender_7_out), .in6(bit_extender_8_out), .in7(bit_extender_9_out),
    .in8({INT_out[7:0], AL_q}), .in9({INT_out[15:8], BL_q}), .in10({INT_out[23:16], CL_q}),
    .in11({INT_out[31:24], DL_q}), .in12(adr_q), .in13(bp_q), .in14(sp_q), .in15(Rem_out), .out(sbus),
    .sel(sregsel));

  // Other names for the same wires on the sheet: dreg[3:0] = dregsel

  // Notes on the sheet:
  //   dregsel
endmodule

module ALU (
  input  [2:0] op,
  input  reset,
  input  [15:0] A,
  input  [15:0] C_IN,
  input  [15:0] B,
  output [15:0] result_Q,
  output [15:0] C_OUT,
  output [7:0] FLAGS
);

  wire adder_1_cout, subtractor_1_bout;
  wire [7:0] comparator_1_gt, not_1_out, not_1_out_2;
  wire [15:0] adder_1_out, and_1_out, bit_extender_1_out, bit_extender_2_out, divider_1_out, divider_1_rem,
       multiplier_1_cout, multiplier_1_out, nor_1_out, or_1_out, pull_resistor_3_node, subtractor_1_out,
       transistor_1_out, xor_1_out;

  Pull_Resistor pull_resistor_1 (.node(C_IN));
  Transistor #(.width(16)) transistor_1 (.in(B), .out(transistor_1_out), .gate(reset));
  Pull_Resistor pull_resistor_2 (.node(transistor_1_out));
  Pull_Resistor pull_resistor_3 (.node(pull_resistor_3_node));
  Transistor #(.width(16)) transistor_2 (.in(A), .out(pull_resistor_3_node), .gate(reset));
  assign and_1_out = pull_resistor_3_node & transistor_1_out;  // AND_Gate and_1, 16 bits wide
  Subtractor #(.width(16)) subtractor_1 (
    .a(pull_resistor_3_node), .b(transistor_1_out), .out(subtractor_1_out), .bin(C_IN[0]),
    .bout(subtractor_1_bout));
  Multiplier #(.width(16)) multiplier_1 (
    .a(pull_resistor_3_node), .b(transistor_1_out), .out(multiplier_1_out), .cin(C_IN),
    .cout(multiplier_1_cout));
  Divider #(.width(16)) divider_1 (
    .a(pull_resistor_3_node), .b(transistor_1_out), .out(divider_1_out), .upper(C_IN), .rem(divider_1_rem));
  Adder #(.width(16)) adder_1 (
    .a(pull_resistor_3_node), .b(transistor_1_out), .out(adder_1_out), .cin(C_IN[0]), .cout(adder_1_cout));
  assign or_1_out = pull_resistor_3_node | transistor_1_out;  // OR_Gate or_1, 16 bits wide
  assign xor_1_out = pull_resistor_3_node ^ transistor_1_out;  // XOR_Gate xor_1, 16 bits wide
  assign nor_1_out = ~(pull_resistor_3_node | transistor_1_out);  // NOR_Gate nor_1, 16 bits wide
  assign bit_extender_1_out = {{15{1'b0}}, subtractor_1_bout};  // Bit_Extender bit_extender_1
  assign bit_extender_2_out = {{15{1'b0}}, adder_1_cout};  // Bit_Extender bit_extender_2
  Multiplexer #(.select(3), .width(16), .enable("false")) multiplexer_1 (
    .in0({16{1'b0}}), .in1(bit_extender_1_out), .in2(multiplier_1_cout), .in3(divider_1_rem),
    .in4(bit_extender_2_out), .in5({16{1'b0}}), .in6({16{1'b0}}), .in7({16{1'b0}}), .out(C_OUT), .sel(op));
  Multiplexer #(.select(3), .width(16), .enable("false")) multiplexer_2 (
    .in0(and_1_out), .in1(subtractor_1_out), .in2(multiplier_1_out), .in3(divider_1_out), .in4(adder_1_out),
    .in5(or_1_out), .in6(xor_1_out), .in7(nor_1_out), .out(result_Q), .sel(op));
  and and_2 (comparator_1_gt[2], not_1_out_2[7], not_1_out_2[6], not_1_out_2[5], not_1_out_2[4], not_1_out_2[3], not_1_out_2[2], not_1_out_2[1], not_1_out_2[0], not_1_out[7], not_1_out[6], not_1_out[5], not_1_out[4], not_1_out[3], not_1_out[2], not_1_out[1], not_1_out[0]);
  Comparator #(.width(16), .mode("unsigned")) comparator_1 (
    .a(pull_resistor_3_node), .b(transistor_1_out), .gt(comparator_1_gt[0]), .eq(comparator_1_gt[1]));  // open: lt
  assign {not_1_out_2, not_1_out} = ~result_Q;  // NOT_Gate not_1, 16 bits wide
  Transistor #(.width(8)) transistor_3 (
    .in({comparator_1_gt[7:4], result_Q[15], comparator_1_gt[2:0]}), .out(FLAGS), .gate(reset));
  Pull_Resistor pull_resistor_4 (.node(FLAGS));

  // Notes on the sheet:
  //   grt
  //   eq
  //   zero
  //   neg
endmodule

module RAM_module (
  input  [15:0] ADDRESS,
  input  [15:0] DATA_IN,
  input  in_3,
  input  in_4,
  input  in_5,
  output [15:0] OUT
);

  wire [15:0] ram_1_data;

  RAM #(.addrWidth(16), .dataWidth(16), .bus("separate")) ram_1 (
    .addr(ADDRESS), .din(DATA_IN), .data(ram_1_data), .str(in_4), .clk(in_3));  // open: sel, ld, clr
  assign OUT = in_5 ? ram_1_data : 16'bz;  // Controlled_Buffer controlled_buffer_1
endmodule

module RND (
  input  [31:0] in_1,
  output [31:0] out_2
);
endmodule

module KeyboardExtender (
  input  [6:0] in_1,
  input  in_2,
  input  in_3,
  input  [31:0] in_4,
  input  [15:0] in_5,
  input  in_6,
  output out_7,
  output [31:0] out_8,
  output out_9,
  output [3:0] out_10,
  output [15:0] out_11,
  output [31:0] out_12
);

  wire and_1_out, and_2_out, buffer_1_out, buffer_2_out, buffer_3_out, buffer_4_out, buffer_5_out,
       buffer_6_out, buffer_7_out, buffer_8_out, comparator_1_eq, comparator_2_eq, comparator_3_eq,
       controlled_buffer_7_out, not_1_out, not_2_out, or_1_out, pull_resistor_1_node, tick2;
  wire [6:0] char, pull_resistor_5_node;
  wire [31:0] controlled_buffer_6_out, pull_resistor_4_node, register_2_q;
  wire [31:7] pull_resistor_3_node;

  Pull_Resistor pull_resistor_1 (.node(pull_resistor_1_node));
  and and_1 (and_1_out, pull_resistor_1_node, not_1_out);
  D_Flip_Flop #(.trigger("low")) d_ff_1 (.clk(in_3), .D(and_1_out), .Q(out_7));  // open: Qn, preset, en, reset
  Comparator #(.width(16)) comparator_1 (.a(in_5), .b(16'h2), .eq(comparator_1_eq));  // open: gt, lt
  D_Flip_Flop d_ff_2 (.clk(in_3), .D(and_2_out), .Q(pull_resistor_1_node));  // open: Qn, preset, en, reset
  and and_2 (and_2_out, comparator_1_eq, in_6);
  Pull_Resistor pull_resistor_2 (.node(comparator_1_eq));
  not not_1 (not_1_out, comparator_3_eq);
  assign out_9 = tick2 ? 1'b1 : 1'bz;  // Controlled_Buffer controlled_buffer_1
  D_Flip_Flop d_ff_3 (
    .clk(in_3), .D(pull_resistor_1_node), .Q(tick2), .reset(register_2_q[0]));  // open: Qn, preset, en
  assign out_11 = tick2 ? 16'h1 : 16'bz;  // Controlled_Buffer controlled_buffer_2
  or or_1 (or_1_out, and_2_out, tick2);
  Pull_Resistor pull_resistor_3 (.node({pull_resistor_3_node, char}));
  assign out_10 = pull_resistor_1_node ? 4'b0001 : 4'bz;  // Controlled_Buffer controlled_buffer_3
  Pull_Resistor pull_resistor_4 (.node(pull_resistor_4_node));
  Comparator #(.width(7)) comparator_2 (.a(char), .b(7'b0001000), .eq(comparator_2_eq));  // open: gt, lt
  Pull_Resistor pull_resistor_5 (.node(pull_resistor_5_node));
  Register #(.width(7)) register_1 (.D(in_1), .en(or_1_out), .Q(char), .clk(in_3));  // open: clr
  buf buffer_1 (buffer_1_out, buffer_3_out);
  buf buffer_2 (buffer_2_out, buffer_4_out);
  buf buffer_3 (buffer_3_out, in_3);
  buf buffer_4 (buffer_4_out, buffer_1_out);
  assign out_8 = pull_resistor_1_node ? {pull_resistor_3_node, char} : 32'bz;  // Controlled_Buffer controlled_buffer_4
  assign out_12 = tick2 ? pull_resistor_4_node : 32'bz;  // Controlled_Buffer controlled_buffer_5
  Multiplexer #(.width(7), .enable("false")) multiplexer_1 (
    .in0(char), .in1({7{1'b0}}), .out(pull_resistor_4_node[6:0]), .sel(comparator_2_eq));
  Comparator #(.width(7)) comparator_3 (.a(pull_resistor_5_node), .b(char), .eq(comparator_3_eq));  // open: gt, lt
  buf buffer_5 (buffer_5_out, buffer_8_out);
  buf buffer_6 (buffer_6_out, buffer_7_out);
  buf buffer_7 (buffer_7_out, buffer_2_out);
  buf buffer_8 (buffer_8_out, buffer_6_out);
  assign controlled_buffer_6_out = pull_resistor_1_node ? in_4 : 32'bz;  // Controlled_Buffer controlled_buffer_6
  Register #(.width(32)) register_2 (
    .D(controlled_buffer_6_out), .Q(register_2_q), .clk(buffer_5_out));  // open: en, clr
  Pull_Resistor pull_resistor_6 (.node(controlled_buffer_6_out));
  Controlled_Buffer controlled_buffer_7 (.in(not_2_out), .out(controlled_buffer_7_out));  // open: en
  Pull_Resistor pull_resistor_7 (.node(controlled_buffer_7_out));
  not not_2 (not_2_out, controlled_buffer_7_out);
  Button button_1 ();  // open: out

  // Notes on the sheet:
  //   INT ADDRESS
endmodule

module TTYextender (
  input  in_1,
  input  [31:0] in_2,
  input  [15:0] in_3,
  input  in_4,
  output out_5,
  output [6:0] out_6,
  output out_7
);

  wire and_1_out, comparator_1_eq;

  Pull_Resistor pull_resistor_1 (.node(in_2));
  Comparator #(.width(16)) comparator_1 (.a(16'h1), .b(in_3), .eq(comparator_1_eq));  // open: gt, lt
  Pull_Resistor pull_resistor_2 (.node(comparator_1_eq));
  Register register_1 (.D(in_2[7:0]), .en(and_1_out), .Q({out_5, out_6}), .clk(in_1));  // open: clr
  and and_1 (and_1_out, comparator_1_eq, in_4);
  Pull_Resistor pull_resistor_3 (.node(out_6));
  D_Flip_Flop d_ff_1 (.clk(in_1), .D(and_1_out), .Q(out_7));  // open: Qn, preset, en, reset

  // Notes on the sheet:
  //   0x0C = clrscr
endmodule

module pinin (
  input  [15:0] in_1,
  input  INT,
  input  [31:0] in_3,
  input  BOOT,
  input  CLK,
  input  in_6,
  input  in_7,
  input  in_8,
  input  in_9,
  input  in_10,
  input  in_11,
  input  in_12,
  input  in_13,
  input  in_14,
  input  in_15,
  input  in_16,
  input  in_17,
  input  in_18,
  input  in_19,
  input  in_20,
  input  in_21,
  input  in_22,
  input  in_23,
  input  in_24,
  input  in_25,
  input  in_26,
  input  in_27,
  input  in_28,
  input  in_29,
  input  in_30,
  input  in_31,
  input  in_32,
  input  in_33,
  input  in_34,
  input  in_35,
  input  in_36,
  input  in_37,
  output [3:0] out_38,
  output [31:0] out_39
);

  wire and_1_out, and_2_out, buffer_1_out, buffer_2_out, buffer_3_out, buffer_4_out, comparator_1_eq,
       multiplexer_1_out, not_1_out, \return ;
  wire [1:0] priority_encoder_1_p3;
  wire [4:0] bit_extender_2_out;
  wire [7:0] bit_extender_1_out, undriven, undriven_2;
  wire [15:0] register_1_q;

  Pull_Resistor pull_resistor_1 (.node(\return ));
  D_Flip_Flop d_ff_1 (.clk(CLK), .D(and_1_out), .Q(\return ));  // open: Qn, preset, en, reset
  Comparator #(.width(16)) comparator_1 (.a(in_1), .b(16'h3), .eq(comparator_1_eq));  // open: gt, lt
  Pull_Resistor pull_resistor_2 (.node(comparator_1_eq));
  Pull_Resistor pull_resistor_3 (.node(INT));
  and and_1 (and_1_out, comparator_1_eq, INT);
  assign out_38 = \return  ? 4'b0001 : 4'bz;  // Controlled_Buffer controlled_buffer_1
  buf buffer_1 (buffer_1_out, multiplexer_1_out);
  Pull_Resistor #(.pull(1)) pull_resistor_4 (.node(buffer_1_out));
  and and_2 (and_2_out, buffer_1_out, ~buffer_2_out);  // AND_Gate
  Multiplexer #(.select(5), .enable("false")) multiplexer_1 (
    .in0(in_6), .in1(in_7), .in2(in_8), .in3(in_9), .in4(in_10), .in5(in_11), .in6(in_12), .in7(in_13),
    .in8(in_14), .in9(in_15), .in10(in_16), .in11(in_17), .in12(in_18), .in13(in_19), .in14(in_20),
    .in15(in_21), .in16(in_22), .in17(in_23), .in18(in_24), .in19(in_25), .in20(in_26), .in21(in_27),
    .in22(in_28), .in23(in_29), .in24(in_30), .in25(in_31), .in26(in_32), .in27(in_33), .in28(in_34),
    .in29(in_35), .in30(in_36), .in31(in_37), .out(multiplexer_1_out), .sel(bit_extender_2_out));
  buf buffer_2 (buffer_2_out, multiplexer_1_out);
  buf buffer_3 (buffer_3_out, multiplexer_1_out);
  Pull_Resistor pull_resistor_5 (.node(buffer_2_out));
  buf buffer_4 (buffer_4_out, multiplexer_1_out);
  Pull_Resistor #(.pull(1)) pull_resistor_6 (.node(buffer_3_out));
  not not_1 (not_1_out, buffer_3_out);
  Pull_Resistor pull_resistor_7 (.node(buffer_4_out));
  // Priority_Encoder #(.select(2)) priority_encoder_1: pin names not known; wires that end beside it: not_1_out, buffer_4_out, priority_encoder_1_p3, and_2_out
  Pull_Resistor pull_resistor_8 (.node(in_3));
  assign out_39 = \return  ? {undriven_2, undriven, register_1_q} : 32'bz;  // Controlled_Buffer controlled_buffer_2
  assign bit_extender_1_out = {{6{1'b0}}, priority_encoder_1_p3};  // Bit_Extender bit_extender_1
  Register register_1 (.D(bit_extender_1_out), .Q(register_1_q[7:0]), .clk(CLK));  // open: en, clr
  Bit_Extender #(.out_width(5)) bit_extender_2 (.in(in_3[7:0]), .out(bit_extender_2_out));

  // Notes on the sheet:
  //   buffer_3 drives only 0 and floats otherwise
  //   buffer_4 drives only 1 and floats otherwise
endmodule

module pinout (
  input  [15:0] in_1,
  input  INT,
  input  [31:0] in_3,
  input  BOOT,
  input  CLK,
  output [3:0] out_6,
  output [31:0] out_7,
  output out_8,
  output out_9,
  output out_10,
  output out_11,
  output out_12,
  output out_13,
  output out_14,
  output out_15,
  output out_16,
  output out_17,
  output out_18,
  output out_19,
  output out_20,
  output out_21,
  output out_22,
  output out_23,
  output out_24,
  output out_25,
  output out_26,
  output out_27,
  output out_28,
  output out_29,
  output out_30,
  output out_31,
  output out_32,
  output out_33,
  output out_34,
  output out_35,
  output out_36,
  output out_37,
  output out_38,
  output out_39
);

  wire and_1_out, and_2_out, buffer_1_out, buffer_2_out, buffer_3_out, buffer_4_out, buffer_5_out,
       comparator_1_eq, comparator_2_eq, controlled_buffer_2_out, d_ff_1_q, decoder_1_out0, decoder_1_out1,
       demultiplexer_1_out0, demultiplexer_1_out1, demultiplexer_1_out2, demultiplexer_1_out3,
       demultiplexer_1_out4, demultiplexer_1_out5, demultiplexer_1_out6, demultiplexer_1_out7,
       demultiplexer_1_out8, demultiplexer_1_out9, demultiplexer_1_out10, demultiplexer_1_out11,
       demultiplexer_1_out12, demultiplexer_1_out13, demultiplexer_1_out14, demultiplexer_1_out15,
       demultiplexer_1_out16, demultiplexer_1_out17, demultiplexer_1_out18, demultiplexer_1_out19,
       demultiplexer_1_out20, demultiplexer_1_out21, demultiplexer_1_out22, demultiplexer_1_out23,
       demultiplexer_1_out24, demultiplexer_1_out25, demultiplexer_1_out26, demultiplexer_1_out27,
       demultiplexer_1_out28, demultiplexer_1_out29, demultiplexer_1_out30, demultiplexer_1_out31, not_1_out,
       pull_resistor_4_node, \return ;
  wire [1:0] bit_extender_1_out;
  wire [3:0] undriven;
  wire [4:0] bit_extender_2_out;
  wire [7:0] register_1_q;
  wire [31:0] undriven_2;

  Pull_Resistor pull_resistor_1 (.node(\return ));
  threestate threestate_1 (.in_2(demultiplexer_1_out0), .in_1(buffer_2_out), .out_4(out_8), .in_3(BOOT));
  Pull_Resistor pull_resistor_2 (.node(CLK));
  threestate threestate_2 (.in_2(demultiplexer_1_out1), .in_1(buffer_2_out), .out_4(out_9), .in_3(BOOT));
  threestate threestate_3 (.in_2(demultiplexer_1_out2), .in_1(buffer_2_out), .out_4(out_10), .in_3(BOOT));
  threestate threestate_4 (.in_2(demultiplexer_1_out3), .in_1(buffer_2_out), .out_4(out_11), .in_3(BOOT));
  threestate threestate_5 (.in_2(demultiplexer_1_out4), .in_1(buffer_2_out), .out_4(out_12), .in_3(BOOT));
  threestate threestate_6 (.in_2(demultiplexer_1_out5), .in_1(buffer_2_out), .out_4(out_13), .in_3(BOOT));
  threestate threestate_7 (.in_2(demultiplexer_1_out6), .in_1(buffer_2_out), .out_4(out_14), .in_3(BOOT));
  Comparator #(.width(16)) comparator_1 (.a(in_1), .b(16'h4), .eq(comparator_1_eq));  // open: gt, lt
  threestate threestate_8 (.in_2(demultiplexer_1_out7), .in_1(buffer_2_out), .out_4(out_15), .in_3(BOOT));
  threestate threestate_9 (.in_2(demultiplexer_1_out8), .in_1(buffer_2_out), .out_4(out_16), .in_3(BOOT));
  Pull_Resistor pull_resistor_3 (.node(INT));
  and and_1 (and_1_out, comparator_1_eq, INT);
  D_Flip_Flop d_ff_1 (.clk(CLK), .D(and_1_out), .Q(d_ff_1_q));  // open: Qn, preset, en, reset
  // Probe on in_3[7:0]
  threestate threestate_10 (.in_2(demultiplexer_1_out9), .in_1(buffer_2_out), .out_4(out_17), .in_3(BOOT));
  threestate threestate_11 (.in_2(demultiplexer_1_out10), .in_1(buffer_2_out), .out_4(out_18), .in_3(BOOT));
  threestate threestate_12 (.in_2(demultiplexer_1_out11), .in_1(buffer_2_out), .out_4(out_19), .in_3(BOOT));
  assign out_6 = \return  ? undriven : 4'bz;  // Controlled_Buffer controlled_buffer_1
  buf buffer_1 (buffer_1_out, buffer_3_out);
  buf buffer_2 (buffer_2_out, buffer_1_out);
  buf buffer_3 (buffer_3_out, buffer_4_out);
  Register register_1 (.D(in_3[7:0]), .Q(register_1_q), .clk(CLK));  // open: en, clr
  threestate threestate_13 (.in_2(demultiplexer_1_out12), .in_1(buffer_2_out), .out_4(out_20), .in_3(BOOT));
  threestate threestate_14 (.in_2(demultiplexer_1_out13), .in_1(buffer_2_out), .out_4(out_21), .in_3(BOOT));
  threestate threestate_15 (.in_2(demultiplexer_1_out14), .in_1(buffer_2_out), .out_4(out_22), .in_3(BOOT));
  Pull_Resistor pull_resistor_4 (.node(pull_resistor_4_node));
  assign controlled_buffer_2_out = decoder_1_out0 ? pull_resistor_4_node : 1'bz;  // Controlled_Buffer controlled_buffer_2
  buf buffer_4 (buffer_4_out, buffer_5_out);
  buf buffer_5 (buffer_5_out, controlled_buffer_2_out);
  Comparator comparator_2 (.a(in_3[7:0]), .b(register_1_q), .eq(comparator_2_eq));  // open: gt, lt
  threestate threestate_16 (.in_2(demultiplexer_1_out15), .in_1(buffer_2_out), .out_4(out_23), .in_3(BOOT));
  threestate threestate_17 (.in_2(demultiplexer_1_out16), .in_1(buffer_2_out), .out_4(out_24), .in_3(BOOT));
  Pull_Resistor pull_resistor_5 (.node(in_3));
  Decoder #(.select(2), .enable("false")) decoder_1 (
    .out0(decoder_1_out0), .out1(decoder_1_out1), .sel(bit_extender_1_out));  // open: out2, out3
  Bit_Extender #(.out_width(2)) bit_extender_1 (.in(in_3[15:8]), .out(bit_extender_1_out));
  not not_1 (not_1_out, pull_resistor_4_node);
  assign controlled_buffer_2_out = decoder_1_out1 ? not_1_out : 1'bz;  // Controlled_Buffer controlled_buffer_3
  threestate threestate_18 (.in_2(demultiplexer_1_out17), .in_1(buffer_2_out), .out_4(out_25), .in_3(BOOT));
  threestate threestate_19 (.in_2(demultiplexer_1_out18), .in_1(buffer_2_out), .out_4(out_26), .in_3(BOOT));
  threestate threestate_20 (.in_2(demultiplexer_1_out19), .in_1(buffer_2_out), .out_4(out_27), .in_3(BOOT));
  assign out_7 = \return  ? undriven_2 : 32'bz;  // Controlled_Buffer controlled_buffer_4
  and and_2 (and_2_out, d_ff_1_q, comparator_2_eq);
  Bit_Extender #(.out_width(5)) bit_extender_2 (.in(register_1_q), .out(bit_extender_2_out));
  threestate threestate_21 (.in_2(demultiplexer_1_out20), .in_1(buffer_2_out), .out_4(out_28), .in_3(BOOT));
  threestate threestate_22 (.in_2(demultiplexer_1_out21), .in_1(buffer_2_out), .out_4(out_29), .in_3(BOOT));
  threestate threestate_23 (.in_2(demultiplexer_1_out22), .in_1(buffer_2_out), .out_4(out_30), .in_3(BOOT));
  threestate threestate_24 (.in_2(demultiplexer_1_out23), .in_1(buffer_2_out), .out_4(out_31), .in_3(BOOT));
  threestate threestate_25 (.in_2(demultiplexer_1_out24), .in_1(buffer_2_out), .out_4(out_32), .in_3(BOOT));
  threestate threestate_26 (.in_2(demultiplexer_1_out25), .in_1(buffer_2_out), .out_4(out_33), .in_3(BOOT));
  threestate threestate_27 (.in_2(demultiplexer_1_out26), .in_1(buffer_2_out), .out_4(out_34), .in_3(BOOT));
  threestate threestate_28 (.in_2(demultiplexer_1_out27), .in_1(buffer_2_out), .out_4(out_35), .in_3(BOOT));
  Demultiplexer #(.select(5), .enable("false")) demultiplexer_1 (
    .out0(demultiplexer_1_out0), .out1(demultiplexer_1_out1), .out2(demultiplexer_1_out2),
    .out3(demultiplexer_1_out3), .out4(demultiplexer_1_out4), .out5(demultiplexer_1_out5),
    .out6(demultiplexer_1_out6), .out7(demultiplexer_1_out7), .out8(demultiplexer_1_out8),
    .out9(demultiplexer_1_out9), .out10(demultiplexer_1_out10), .out11(demultiplexer_1_out11),
    .out12(demultiplexer_1_out12), .out13(demultiplexer_1_out13), .out14(demultiplexer_1_out14),
    .out15(demultiplexer_1_out15), .out16(demultiplexer_1_out16), .out17(demultiplexer_1_out17),
    .out18(demultiplexer_1_out18), .out19(demultiplexer_1_out19), .out20(demultiplexer_1_out20),
    .out21(demultiplexer_1_out21), .out22(demultiplexer_1_out22), .out23(demultiplexer_1_out23),
    .out24(demultiplexer_1_out24), .out25(demultiplexer_1_out25), .out26(demultiplexer_1_out26),
    .out27(demultiplexer_1_out27), .out28(demultiplexer_1_out28), .out29(demultiplexer_1_out29),
    .out30(demultiplexer_1_out30), .out31(demultiplexer_1_out31), .in(and_2_out), .sel(bit_extender_2_out));
  threestate threestate_29 (.in_2(demultiplexer_1_out28), .in_1(buffer_2_out), .out_4(out_36), .in_3(BOOT));
  threestate threestate_30 (.in_2(demultiplexer_1_out29), .in_1(buffer_2_out), .out_4(out_37), .in_3(BOOT));
  threestate threestate_31 (.in_2(demultiplexer_1_out30), .in_1(buffer_2_out), .out_4(out_38), .in_3(BOOT));
  threestate threestate_32 (.in_2(demultiplexer_1_out31), .in_1(buffer_2_out), .out_4(out_39), .in_3(BOOT));
endmodule

module threestate (
  input  in_1,
  input  in_2,
  input  in_3,
  output out_4
);

  wire and_1_out, buffer_2_out, buffer_3_out, buffer_4_out, controlled_buffer_1_out, decoder_1_out1,
       decoder_1_out2, not_1_out, pull_resistor_2_node, pull_resistor_7_node, pull_resistor_8_node;
  wire [1:0] priority_encoder_1_p3, register_1_q;

  Pull_Resistor pull_resistor_1 (.node(in_2));
  Pull_Resistor #(.pull(1)) pull_resistor_2 (.node(pull_resistor_2_node));
  buf buffer_1 (pull_resistor_2_node, in_1);
  buf buffer_2 (buffer_2_out, in_1);
  Pull_Resistor pull_resistor_3 (.node(buffer_2_out));
  and and_1 (and_1_out, pull_resistor_2_node, ~buffer_2_out);  // AND_Gate
  buf buffer_3 (buffer_3_out, in_1);
  buf buffer_4 (buffer_4_out, in_1);
  Pull_Resistor #(.pull(1)) pull_resistor_4 (.node(buffer_3_out));
  not not_1 (not_1_out, buffer_3_out);
  Pull_Resistor pull_resistor_5 (.node(buffer_4_out));
  // Priority_Encoder #(.select(2)) priority_encoder_1: pin names not known; wires that end beside it: and_1_out, buffer_4_out, priority_encoder_1_p3, not_1_out
  Register #(.width(2)) register_1 (.D(priority_encoder_1_p3), .Q(register_1_q), .clk(in_2), .clr(in_3));  // open: en
  Pull_Resistor pull_resistor_6 (.node(in_3));
  Decoder #(.select(2), .enable("false")) decoder_1 (
    .out1(decoder_1_out1), .out2(decoder_1_out2), .sel(register_1_q));  // open: out0, out3
  assign controlled_buffer_1_out = decoder_1_out2 ? pull_resistor_7_node : 1'bz;  // Controlled_Buffer controlled_buffer_1
  Pull_Resistor pull_resistor_7 (.node(pull_resistor_7_node));
  Pull_Resistor #(.pull(1)) pull_resistor_8 (.node(pull_resistor_8_node));
  assign controlled_buffer_1_out = decoder_1_out1 ? pull_resistor_8_node : 1'bz;  // Controlled_Buffer controlled_buffer_2
  ConsumeError consumeerror_1 (.in_1(controlled_buffer_1_out), .out_2(out_4));

  // Notes on the sheet:
  //   buffer_3 drives only 0 and floats otherwise
  //   buffer_4 drives only 1 and floats otherwise
endmodule

module twoway (
  input  in_1,
  input  in_2,
  output out_3,
  output out_4
);

  wire buffer_1_out, buffer_2_out, buffer_3_out, buffer_4_out, buffer_6_out, buffer_7_out, buffer_8_out,
       buffer_9_out, buffer_10_out, consumeerror_2_out_2, consumeerror_3_out_2, notfloat_1_out_2,
       notfloat_2_out_2, pull_resistor_1_node, transistor_1_out, transistor_2_out, transistor_3_out,
       transistor_4_out, undriven;

  Transistor #(.gate("br")) transistor_1 (.in(in_1), .out(transistor_1_out), .gate(pull_resistor_1_node));
  buf buffer_1 (buffer_1_out, transistor_1_out);
  buf buffer_2 (buffer_2_out, buffer_1_out);
  Transistor #(.gate("br")) transistor_2 (.in(buffer_2_out), .out(transistor_2_out), .gate(consumeerror_2_out_2));
  buf buffer_3 (buffer_3_out, transistor_2_out);
  buf buffer_4 (buffer_4_out, buffer_3_out);
  ConsumeError consumeerror_1 (.in_1(buffer_4_out), .out_2(out_4));
  Pull_Resistor #(.pull(1)) pull_resistor_1 (.node(pull_resistor_1_node));
  buf buffer_5 (pull_resistor_1_node, consumeerror_2_out_2);
  ConsumeError consumeerror_2 (.in_1(undriven), .out_2(consumeerror_2_out_2));
  NotFloat notfloat_1 (.out_2(notfloat_1_out_2), .in_1(transistor_2_out));
  NotFloat notfloat_2 (.out_2(notfloat_2_out_2), .in_1(transistor_3_out));
  ConsumeError consumeerror_3 (.in_1(notfloat_1_out_2), .out_2(consumeerror_3_out_2));
  ConsumeError consumeerror_4 (.in_1(buffer_6_out), .out_2(out_3));
  buf buffer_6 (buffer_6_out, buffer_7_out);
  buf buffer_7 (buffer_7_out, transistor_3_out);
  Transistor transistor_3 (.in(buffer_8_out), .out(transistor_3_out), .gate(consumeerror_3_out_2));
  buf buffer_8 (buffer_8_out, buffer_9_out);
  buf buffer_9 (buffer_9_out, buffer_10_out);
  buf buffer_10 (buffer_10_out, transistor_4_out);
  Transistor transistor_4 (.in(in_2), .out(transistor_4_out), .gate(consumeerror_3_out_2));
endmodule

module ConsumeError (
  input  in_1,
  output out_2
);

  wire buffer_3_out, buffer_4_out, buffer_5_out, buffer_6_out, buffer_7_out, buffer_8_out, buffer_9_out,
       d_ff_1_qn, pull_resistor_1_node, pull_resistor_2_node, transistor_1_out;

  // Buffer buffer_1 has open pins: in=open, out=in_1
  Transistor transistor_1 (.in(pull_resistor_2_node), .out(transistor_1_out), .gate(pull_resistor_1_node));
  Pull_Resistor pull_resistor_1 (.node(pull_resistor_1_node));
  Pull_Resistor #(.pull(1)) pull_resistor_2 (.node(pull_resistor_2_node));
  buf buffer_2 (pull_resistor_1_node, in_1);
  buf buffer_3 (buffer_3_out, in_1);
  D_Flip_Flop d_ff_1 (.Qn(d_ff_1_qn), .preset(1'b1), .reset(transistor_1_out));  // open: clk, D, Q, en
  buf buffer_4 (buffer_4_out, buffer_3_out);
  buf buffer_5 (buffer_5_out, buffer_7_out);
  buf buffer_6 (buffer_6_out, buffer_5_out);
  buf buffer_7 (buffer_7_out, buffer_4_out);
  Pull_Resistor pull_resistor_3 (.node(d_ff_1_qn));
  buf buffer_8 (buffer_8_out, buffer_9_out);
  buf buffer_9 (buffer_9_out, buffer_6_out);
  Transistor #(.\type ("n")) transistor_2 (.in(buffer_8_out), .out(out_2), .gate(d_ff_1_qn));

  // Notes on the sheet:
  //   buffer_1 drives only 0 and floats otherwise
  //   buffer_2 drives only 0 and floats otherwise
endmodule

module NotFloat (
  input  in_1,
  output out_2
);

  wire pull_resistor_1_node, pull_resistor_2_node, pull_resistor_3_node, pull_resistor_4_node;

  Pull_Resistor pull_resistor_1 (.node(pull_resistor_1_node));
  buf buffer_1 (pull_resistor_1_node, pull_resistor_3_node);
  or or_1 (out_2, pull_resistor_1_node, pull_resistor_2_node);
  Pull_Resistor pull_resistor_2 (.node(pull_resistor_2_node));
  not not_1 (pull_resistor_2_node, pull_resistor_4_node);
  Pull_Resistor pull_resistor_3 (.node(pull_resistor_3_node));
  buf buffer_2 (pull_resistor_3_node, in_1);
  Pull_Resistor #(.pull(1)) pull_resistor_4 (.node(pull_resistor_4_node));
  buf buffer_3 (pull_resistor_4_node, in_1);

  // Notes on the sheet:
  //   buffer_2 drives only 1 and floats otherwise
endmodule

module PowerBox (
  input  [15:0] in_1,
  input  INT,
  input  [31:0] in_3,
  output out_4,
  output out_5
);

  wire and_1_out, comparator_1_eq, comparator_2_eq, comparator_3_eq;

  Pull_Resistor pull_resistor_1 (.node(in_1));
  Comparator #(.width(16)) comparator_1 (.a(in_1), .b({16{1'b1}}), .eq(comparator_1_eq));  // open: gt, lt
  Pull_Resistor pull_resistor_2 (.node(INT));
  and and_1 (and_1_out, comparator_1_eq, INT);
  Pull_Resistor pull_resistor_3 (.node(in_3));
  Comparator comparator_2 (.a(in_3[7:0]), .b({8{1'b0}}), .eq(comparator_2_eq));  // open: gt, lt
  assign out_4 = and_1_out ? comparator_2_eq : 1'bz;  // Controlled_Buffer controlled_buffer_1
  assign out_5 = and_1_out ? comparator_3_eq : 1'bz;  // Controlled_Buffer controlled_buffer_2
  Comparator comparator_3 (.a(in_3[7:0]), .b(8'h1), .eq(comparator_3_eq));  // open: gt, lt
  Pull_Resistor pull_resistor_4 (.node(out_4));
  Pull_Resistor pull_resistor_5 (.node(out_5));
endmodule

module increment16bit (
  input  [15:0] in_1,
  output [15:0] out_2
);

  wire pull_resistor_1_node;
  wire [15:0] pull_resistor_2_node;

  Pull_Resistor #(.pull(1)) pull_resistor_1 (.node(pull_resistor_1_node));
  Pull_Resistor pull_resistor_2 (.node(pull_resistor_2_node));
  Adder #(.width(16)) adder_1 (
    .a(in_1), .b(pull_resistor_2_node), .out(out_2), .cin(pull_resistor_1_node));  // open: cout
endmodule
